# Fritzing sketch diagramCircuit (saved by Fritzing 0.9.3b)

parts:
  U1 = NodeMCU V1.0
  Transceiver1 = nRF24L01 [package=module]
  DHT1 = DHT11 Humitidy and Temperature Sensor

nets:
  N1: U1.D0, U1.RST, U1.3V3#19
  GND: U1.D1, U1.GND, U1.D5, U1.D6, U1.D7, U1.D8, Transceiver1.GND, Transceiver1.CSN, Transceiver1.SCK, Transceiver1.MOSI, Transceiver1.MISO
  N2: U1.D2, DHT1.DATA
  N3: U1.D4, Transceiver1.CE
  N4: U1.3V3#5, Transceiver1.VCC

custom parts:
  NodeMCU V1.0: ESP8266 based NodeMCU V1.0
  nRF24L01: nRF24L01 module
  DHT11 Humitidy and Temperature Sensor: DHT11 Humidity and Temperature Sensor
