# Fritzing sketch diagramCircuitSlave (saved by Fritzing 0.9.3b)

parts:
  U2 = NodeMCU V1.0
  Transceiver2 = nRF24L01 [package=module]

nets:
  N1: U2.D0, U2.RST, U2.3V3#19
  GND: U2.D1, U2.GND, U2.D5, U2.D6, U2.D7, U2.D8, Transceiver2.GND, Transceiver2.CSN, Transceiver2.SCK, Transceiver2.MOSI, Transceiver2.MISO
  N2: U2.D4, Transceiver2.CE
  N3: U2.3V3#5, Transceiver2.VCC

custom parts:
  NodeMCU V1.0: ESP8266 based NodeMCU V1.0
  nRF24L01: nRF24L01 module
